# Fritzing sketch run_by_button (saved by Fritzing 0.8.0b)
breadboards: 1

parts:
  Raspberry_Pi1 = Raspberry Pi
  LED1 = LED - 5mm [color="Red (633nm)" package="5 mm [THT]"]
  S1 = Pushbutton [package="[THT]"]
  R2 = Resistor [tolerance=±5% resistance=10k package=THT]
  R1 = Resistor [tolerance=±5% resistance=470 package=THT]

nets:
  N1: Raspberry_Pi1.5V, Raspberry_Pi1.GPIO1, S1.Pin_3, S1.Pin_4, R2.Pin_1
  N2: Raspberry_Pi1.GND, R2.Pin_0, R1.Pin_0
  N3: Raspberry_Pi1.GPIO0, LED1.anode
  N4: LED1.cathode, R1.Pin_1
  N5: S1.Pin_1, S1.Pin_2

notes:
  serial console output
  470 ohm
  10k ohm
